# Fritzing sketch chapa (saved by Fritzing 0.9.3b)
circuit board: 8.46667cm x 5.64444cm

parts:
  U1 = NodeMCU V1.0
  LED1 = RGB LED (com. cathode, rgb) [package="5 mm [THT]"]
  Part1 = RFID-RC522-v3
  VCC1 = Battery
  J1 = Basic Servo

nets:
  N1: U1.D0, LED1.blue_anode
  N2: U1.D1, Part1.RST
  N3: U1.D2, Part1.SDA
  N4: U1.D3, LED1.green_anode
  N5: U1.D4, J1.pulse
  3V3: U1.3V3, Part1.3.3V
  GND: U1.GND, LED1.common_cathode, Part1.GND, VCC1.-, J1.gnd
  N6: U1.D5, Part1.SCK
  N7: U1.D6, Part1.MISO
  N8: U1.D7, Part1.MOSI
  N9: U1.D8, LED1.red_anode
  VIN: U1.Vin, VCC1.+, J1.vcc

custom parts:
  NodeMCU V1.0: ESP8266 based NodeMCU
  RFID-RC522-v3: A simple China made RFID-RC522 Reader (6x4 cm); do check the pin labels, as this is a MFRC522 based clone.
